// Logisim project jk.circ as structural Verilog: 1 circuit, main circuit main
module main (
);

  wire clock_1_out, j_k_ff_1_q, j_k_ff_2_q;

  Clock clock_1 (.out(clock_1_out));
  J_K_Flip_Flop #(.trigger("falling")) j_k_ff_1 (
    .J(1'b1), .clk(clock_1_out), .K(1'b1), .Q(j_k_ff_1_q));  // open: Qn, preset, en, reset
  J_K_Flip_Flop #(.trigger("falling")) j_k_ff_2 (
    .J(1'b1), .clk(j_k_ff_1_q), .K(1'b1), .Q(j_k_ff_2_q));  // open: Qn, preset, en, reset
  J_K_Flip_Flop #(.trigger("falling")) j_k_ff_3 (
    .J(1'b1), .clk(j_k_ff_2_q), .K(1'b1));  // open: Q, Qn, preset, en, reset
endmodule
