// Logisim project test1.circ as structural Verilog: 1 circuit, main circuit main
module main (
  output out_1,
  output out_2,
  output out_3
);

  wire and_1_out, clock_1_out, not_1_out, not_2_out, not_3_out, not_4_out, not_5_out;

  Clock clock_1 (.out(clock_1_out));
  not not_1 (not_1_out, clock_1_out);
  J_K_Flip_Flop j_k_ff_1 (.J(1'b1), .clk(not_1_out), .K(1'b1), .Q(out_1), .reset(not_5_out));  // open: Qn, preset, en
  J_K_Flip_Flop j_k_ff_2 (.J(1'b1), .clk(not_2_out), .K(1'b1), .Q(out_2), .reset(not_5_out));  // open: Qn, preset, en
  not not_2 (not_2_out, out_1);
  not not_3 (not_3_out, out_2);
  J_K_Flip_Flop j_k_ff_3 (.J(1'b1), .clk(not_3_out), .K(1'b1), .Q(out_3), .reset(not_5_out));  // open: Qn, preset, en
  not not_4 (not_4_out, and_1_out);
  and and_1 (and_1_out, out_3, out_1);
  not not_5 (not_5_out, not_4_out);
endmodule
