// Logisim project 2.1.2.circ as structural Verilog: 1 circuit, main circuit main
module main (
  input  a,
  input  b,
  input  c,
  output x,
  output y
);

  wire and_1_out, not_1_out, not_2_out, not_3_out, not_4_out;

  not not_1 (not_1_out, a);
  not not_2 (not_2_out, b);
  not not_3 (not_3_out, b);
  and and_1 (and_1_out, not_1_out, not_2_out);
  not not_4 (not_4_out, c);
  and and_2 (y, not_3_out, c);
  or or_1 (x, and_1_out, not_4_out);
endmodule
